// Logisim project mapa.circ as structural Verilog: 1 circuit, main circuit main
module main (
  input  I3,
  input  I2,
  input  I1,
  input  I0
);

  wire and_1_out, and_2_out, and_3_out, and_4_out, and_5_out, and_6_out, and_7_out, and_8_out, and_9_out,
       and_10_out, and_11_out, and_12_out, and_13_out, and_14_out, and_15_out, and_16_out, and_17_out,
       and_18_out, and_19_out, and_20_out, and_21_out, and_22_out, and_23_out, and_24_out, and_25_out,
       and_26_out, and_27_out, and_28_out, and_29_out, and_30_out, not_1_out, not_2_out, not_3_out,
       not_4_out, or_1_out, or_2_out, or_3_out, or_4_out, or_5_out, or_6_out, or_7_out;

  not not_1 (not_1_out, I3);
  not not_2 (not_2_out, I2);
  not not_3 (not_3_out, I0);
  not not_4 (not_4_out, I1);
  and and_1 (and_1_out, I2, not_1_out);
  and and_2 (and_2_out, not_3_out, not_1_out);
  and and_3 (and_3_out, not_3_out, I1);
  and and_4 (and_4_out, I0, not_2_out, I3);
  and and_5 (and_5_out, I0, not_4_out, I3);
  and and_6 (and_6_out, not_4_out, not_1_out);
  and and_7 (and_7_out, not_3_out, not_1_out);
  and and_8 (and_8_out, not_3_out, not_4_out);
  and and_9 (and_9_out, I2, I3);
  and and_10 (and_10_out, I0, I1, I3);
  and and_11 (and_11_out, not_3_out, not_4_out);
  and and_12 (and_12_out, I2, I3);
  and and_13 (and_13_out, not_4_out, not_1_out);
  and and_14 (and_14_out, not_3_out, not_1_out);
  and and_15 (and_15_out, not_3_out, I1);
  and and_16 (and_16_out, not_2_out, I3);
  and and_17 (and_17_out, not_3_out, not_2_out);
  and and_18 (and_18_out, I1, I2, not_1_out);
  and and_19 (and_19_out, not_3_out, I3);
  and and_20 (and_20_out, not_3_out, not_4_out);
  and and_21 (and_21_out, not_4_out, not_1_out);
  and and_22 (and_22_out, not_4_out, I2);
  and and_23 (and_23_out, I0, I2, I3);
  and and_24 (and_24_out, not_3_out, not_2_out, I3);
  and and_25 (and_25_out, not_3_out, not_4_out);
  and and_26 (and_26_out, not_4_out, not_1_out);
  and and_27 (and_27_out, I1, not_2_out, I3);
  and and_28 (and_28_out, I0, I2, I3);
  and and_29 (and_29_out, I0, I1);
  and and_30 (and_30_out, I0, I2);
  or or_1 (or_1_out, and_1_out, and_2_out, and_3_out, and_4_out, and_5_out);
  or or_2 (or_2_out, and_6_out, and_7_out, and_8_out, and_9_out, and_10_out);
  or or_3 (or_3_out, and_11_out, and_12_out, and_13_out, and_14_out);
  or or_4 (or_4_out, and_15_out, and_16_out, and_17_out, and_18_out, and_19_out);
  or or_5 (or_5_out, and_20_out, and_21_out, and_22_out, and_23_out, and_24_out);
  or or_6 (or_6_out, and_25_out, and_26_out, and_27_out, and_28_out);
  or or_7 (or_7_out, and_29_out, and_30_out);
  LED b (.in(or_2_out));
  LED a (.in(or_1_out));
  LED c (.in(or_3_out));
  LED d (.in(or_4_out));
  LED e (.in(or_5_out));
  LED f (.in(or_6_out));
  LED g (.in(or_7_out));

  // Notes on the sheet:
  //   Inputs
  //   Minterminos2 para a
  //   Minterminos para b
  //   Minterminos para c
  //   Minterminos para d
  //   Minterminos para e
  //   Minterminos para f
  //   Minterminos para g
  //   Outputs
endmodule
