// Logisim project Secuencia.circ as structural Verilog: 3 circuits, main circuit main
module main (
);

  wire logica_de_estados_b0, logica_de_estados_b1, logica_de_estados_b2, logica_de_estados_b3,
       Logica_de_salida_a, Logica_de_salida_b, Logica_de_salida_c, Logica_de_salida_d, Logica_de_salida_e,
       Logica_de_salida_f, Logica_de_salida_g;

  logica_de_estados logica_de_estados (
    .B0(logica_de_estados_b0), .B1(logica_de_estados_b1), .B2(logica_de_estados_b2), .B3(logica_de_estados_b3));
  Logica_de_salida Logica_de_salida (
    .B3(logica_de_estados_b3), .B2(logica_de_estados_b2), .B1(logica_de_estados_b1),
    .B0(logica_de_estados_b0), .a(Logica_de_salida_a), .b(Logica_de_salida_b), .c(Logica_de_salida_c),
    .d(Logica_de_salida_d), .e(Logica_de_salida_e), .f(Logica_de_salida_f), .g(Logica_de_salida_g));
  _7_Segment_Display u_7_segment_display_1 (
    .g(Logica_de_salida_g), .f(Logica_de_salida_f), .a(Logica_de_salida_a), .b(Logica_de_salida_b),
    .e(Logica_de_salida_e), .d(Logica_de_salida_d), .c(Logica_de_salida_c));  // open: dp
endmodule

module Logica_de_salida (
  input  B3,
  input  B2,
  input  B1,
  input  B0,
  output a,
  output b,
  output c,
  output d,
  output e,
  output f,
  output g
);

  wire and_1_out, and_2_out, and_3_out, and_4_out, and_5_out, and_6_out, and_7_out, and_8_out, and_9_out,
       and_10_out, and_11_out, and_12_out, and_13_out, and_14_out, and_15_out, and_16_out, and_17_out,
       and_18_out, and_19_out, and_20_out, and_21_out, and_22_out, and_23_out, and_24_out, and_25_out,
       and_26_out, and_27_out, and_28_out, not_1_out, not_2_out, not_3_out, not_4_out;

  not not_1 (not_1_out, B2);
  not not_2 (not_2_out, B3);
  not not_3 (not_3_out, B1);
  not not_4 (not_4_out, B0);
  and and_1 (and_1_out, B1, not_1_out, not_2_out);
  and and_2 (and_2_out, B0, B2, not_2_out);
  and and_3 (and_3_out, not_4_out, B1, B3);
  and and_4 (and_4_out, not_4_out, B2, B3);
  and and_5 (and_5_out, B0, B1);
  and and_6 (and_6_out, not_4_out, not_3_out, B2);
  and and_7 (and_7_out, B1, B2, B3);
  and and_8 (and_8_out, not_4_out, not_3_out, B2);
  and and_9 (and_9_out, B0, not_3_out, not_2_out);
  and and_10 (and_10_out, B0, B1, B2);
  and and_11 (and_11_out, B0, B1, B3);
  and and_12 (and_12_out, B1, B2, B3);
  and and_13 (and_13_out, not_1_out, B3);
  and and_14 (and_14_out, B0, not_3_out, B2);
  and and_15 (and_15_out, B0, B1, not_1_out);
  and and_16 (and_16_out, not_4_out, B1, B2, not_2_out);
  and and_17 (and_17_out, B0, B1);
  and and_18 (and_18_out, not_3_out, B3);
  and and_19 (and_19_out, B1, not_2_out);
  and and_20 (and_20_out, not_4_out, not_3_out);
  and and_21 (and_21_out, B2, not_2_out);
  and and_22 (and_22_out, not_1_out, B3);
  and and_23 (and_23_out, B0, B3);
  and and_24 (and_24_out, not_4_out, not_2_out);
  and and_25 (and_25_out, B0, not_2_out);
  and and_26 (and_26_out, not_4_out, not_3_out, B2);
  and and_27 (and_27_out, B0, B1, B2);
  and and_28 (and_28_out, not_4_out, B1, not_1_out);
  or or_1 (a, and_1_out, and_2_out, and_3_out, and_4_out);
  or or_2 (b, and_5_out, and_6_out, and_7_out);
  or or_3 (c, and_8_out, and_9_out, and_10_out, and_11_out, and_12_out);
  or or_4 (d, and_13_out, and_14_out, and_15_out, and_16_out);
  or or_5 (e, not_1_out, and_17_out, and_18_out, and_19_out);
  or or_6 (f, and_20_out, and_21_out, and_22_out, and_23_out, and_24_out);
  or or_7 (g, and_25_out, and_26_out, and_27_out, and_28_out);
endmodule

module logica_de_estados (
  output B0,
  output B1,
  output B2,
  output B3
);

  wire and_1_out, and_2_out, and_3_out, and_4_out, and_5_out, and_6_out, and_7_out, and_8_out, and_9_out,
       B0_qn, B1_qn, B2_qn, clock_1_out, d_ff_1_qn, or_1_out, or_2_out, or_3_out;

  Clock clock_1 (.out(clock_1_out));
  D_Flip_Flop u_B0 (.clk(clock_1_out), .D(B0_qn), .Q(B0), .Qn(B0_qn));  // open: preset, en, reset
  D_Flip_Flop u_B1 (.clk(clock_1_out), .D(or_1_out), .Q(B1), .Qn(B1_qn));  // open: preset, en, reset
  D_Flip_Flop u_B2 (.clk(clock_1_out), .D(or_2_out), .Q(B2), .Qn(B2_qn));  // open: preset, en, reset
  D_Flip_Flop d_ff_1 (.clk(clock_1_out), .D(or_3_out), .Q(B3), .Qn(d_ff_1_qn));  // open: preset, en, reset
  and and_1 (and_1_out, B0, B1_qn);
  or or_1 (or_1_out, and_1_out, and_2_out);
  and and_2 (and_2_out, B1, B0_qn);
  and and_3 (and_3_out, B2, B1_qn);
  and and_4 (and_4_out, B2, B0_qn);
  and and_5 (and_5_out, B2_qn, B0, B1);
  and and_6 (and_6_out, B3, B2_qn);
  and and_7 (and_7_out, B3, B1_qn);
  and and_8 (and_8_out, B3, B0_qn);
  and and_9 (and_9_out, B0, B1, B2, d_ff_1_qn);
  or or_2 (or_2_out, and_3_out, and_4_out, and_5_out);
  or or_3 (or_3_out, and_6_out, and_7_out, and_8_out, and_9_out);
endmodule
